// Logisim project alu.circ as structural Verilog: 1 circuit, main circuit ALU
module ALU (
  input  Op,
  input  carry_in,
  input  [31:0] Input_1,
  input  [31:0] Input_2,
  input  [2:0] select,
  output carry_out,
  output [31:0] Ouput,
  output Zero
);

  wire adder_1_overflow, and_2_out, or_2_out;
  wire [4:0] bit_extender_1_out;
  wire [31:0] adder_1_output, and_1_out, or_1_out, right_shift_1_out_4, shifter_1_out, slt_1_output,
       sltu_1_out_4, xor_1_out;

  Bit_Extender #(.in_width(32), .out_width(5)) bit_extender_1 (.in(Input_2), .out(bit_extender_1_out));
  assign xor_1_out = Input_1 ^ Input_2;  // XOR_Gate xor_1, 32 bits wide
  Shifter #(.width(32)) shifter_1 (.in(Input_1), .\dist (bit_extender_1_out), .out(shifter_1_out));
  assign and_1_out = Input_1 & Input_2;  // AND_Gate and_1, 32 bits wide
  adder adder_1 (
    .carry(carry_in), .Input_1(Input_1), .Input_2(Input_2), .Select(Op), .overflow(adder_1_overflow),
    .\output (adder_1_output));
  slt slt_1 (.carry_in(carry_in), .input_1(Input_1), .input_2(Input_2), .\output (slt_1_output));  // open: carry_out
  sltu sltu_1 (.in_1(Input_1), .in_2(Input_2), .carry_in(carry_in), .out_4(sltu_1_out_4));  // open: carry_out
  right_shift right_shift_1 (.input_1(Input_1), .input_2(Input_2), .select_input(Op), .out_4(right_shift_1_out_4));
  assign or_1_out = Input_1 | Input_2;  // OR_Gate or_1, 32 bits wide
  Multiplexer #(.select(3), .width(32), .enable("false")) multiplexer_1 (
    .in0(adder_1_output), .in1(shifter_1_out), .in2(slt_1_output), .in3(sltu_1_out_4), .in4(xor_1_out),
    .in5(right_shift_1_out_4), .in6(or_1_out), .in7(and_1_out), .out(Ouput), .sel(select));
  and and_2 (and_2_out, ~select[0], ~select[1], ~select[2]);  // AND_Gate
  and and_3 (carry_out, adder_1_overflow, and_2_out);
  or or_2 (or_2_out, Ouput[0], Ouput[1], Ouput[2], Ouput[3], Ouput[4], Ouput[5], Ouput[6], Ouput[7], Ouput[8], Ouput[9], Ouput[10], Ouput[11], Ouput[12], Ouput[13], Ouput[14], Ouput[15], Ouput[16], Ouput[17], Ouput[18], Ouput[19], Ouput[20], Ouput[21], Ouput[22], Ouput[23], Ouput[24], Ouput[25], Ouput[26], Ouput[27], Ouput[28], Ouput[29], Ouput[30], Ouput[31]);
  not not_1 (Zero, or_2_out);
endmodule
