// Logisim project control unit revised.circ as structural Verilog: 1 circuit, main circuit main
module main (
  input  clk,
  input  [31:0] alu_out,
  input  [31:0] inst_in,
  input  z_in,
  input  c_in,
  input  Sub_in,
  output [2:0] ALU_Op,
  output ALU_Src1,
  output [1:0] ALU_Src2,
  output PC_Src,
  output Sub,
  output I_Or_D,
  output Mem_Read,
  output IR_Load,
  output [31:0] imm,
  output ALU_Out_Ld,
  output A_Load,
  output B_Load,
  output [4:0] rs1,
  output [4:0] rs2,
  output [4:0] rd,
  output Mem2Reg,
  output Reg_Write,
  output Reg_Src_2,
  output PC_Load,
  output mdr_load,
  output Mem_Write,
  output [1:0] Width,
  output extend,
  output halt
);

  wire and_1_out, and_2_out, and_3_out, and_4_out, and_5_out, and_6_out, and_10_out, and_11_out, and_12_out,
       and_13_out, and_14_out, and_15_out, and_16_out, and_17_out, and_18_out, and_19_out, and_20_out,
       and_26_out, and_27_out, and_28_out, and_29_out, and_38_out, and_39_out, and_40_out, and_43_out,
       and_47_out, AUIPC, BRANCH, branch_z, custom_ALU_Op, Decode, decoder_1_out0, decoder_1_out1,
       decoder_1_out2, decoder_1_out3, decoder_1_out4, decoder_2_out0, decoder_2_out1, decoder_2_out4,
       decoder_2_out5, decoder_2_out6, decoder_2_out7, decoder_3_out0, decoder_3_out4, decoder_3_out6,
       decoder_4_out0, decoder_4_out1, decoder_4_out3, decoder_5_out0, decoder_5_out1, decoder_5_out3,
       decoder_5_out4, decoder_5_out5, I_Type, JAL, JALR, LOAD, LUI, MISC_MEM, multiplexer_2_out,
       multiplexer_5_out, multiplexer_7_out, multiplexer_9_out, nor_1_out, not_1_out, OP, OP_IMM, or_1_out,
       or_2_out, or_3_out, or_4_out, or_6_out, or_8_out, or_9_out, or_11_out, or_12_out, or_13_out,
       or_14_out, or_16_out, STORE, Sub_in_srai, SYSTEM, tty_write, U_Type, valid_opc, xnor_2_out;
  wire [1:0] bit_extender_1_out, bit_extender_5_out, multiplexer_3_out, multiplexer_4_out, multiplexer_6_out,
       multiplexer_8_out, multiplexer_10_out, multiplexer_11_out, multiplexer_12_out, multiplexer_13_out,
       multiplexer_14_out, multiplexer_18_out;
  wire [2:0] and_7_out, and_8_out, and_9_out, bit_extender_2_out, bit_extender_3_out, bit_extender_4_out,
       branch_type, counter_1_q, custom_bus_ALU_Op, multiplexer_17_out, xnor_1_out, xnor_3_out;
  wire [4:0] multiplexer_16_out;
  wire [6:0] multiplexer_15_out, tty_input;
  wire [19:0] and_41_out, and_42_out, and_44_out, and_45_out, and_46_out, bit_extender_6_out,
       bit_extender_7_out, bit_extender_8_out, bit_extender_9_out, bit_extender_10_out, bit_extender_13_out,
       imm_i, imm_s, imm_sb, or_17_out, or_18_out;
  wire [30:0] bit_extender_11_out;
  wire [31:0] bit_extender_12_out;

  Decoder #(.select(3)) decoder_1 (
    .out0(decoder_1_out0), .out1(decoder_1_out1), .out2(decoder_1_out2), .out3(decoder_1_out3),
    .out4(decoder_1_out4), .sel(counter_1_q));  // open: out5, out6, out7, en
  Counter #(.width(3), .max('h4), .trigger("falling")) counter_1 (
    .Q(counter_1_q), .clk(clk));  // open: load, D, count, carry, clr
  buf buffer_1 (PC_Src, decoder_1_out0);
  buf buffer_2 (Decode, decoder_1_out1);
  Multiplexer #(.width(3), .enable("false")) multiplexer_1 (
    .in0(inst_in[14:12]), .in1(custom_bus_ALU_Op), .out(ALU_Op), .sel(custom_ALU_Op));
  buf buffer_3 (Mem_Read, decoder_1_out0);
  buf buffer_4 (A_Load, decoder_1_out1);
  buf buffer_5 (B_Load, decoder_1_out1);
  and and_1 (and_1_out, decoder_1_out2, OP);
  buf buffer_6 (ALU_Out_Ld, and_1_out);
  buf buffer_7 (ALU_Src1, and_1_out);
  Multiplexer #(.enable("false")) multiplexer_2 (.in1(Sub_in), .out(multiplexer_2_out), .sel(and_1_out));  // open: in0
  buf buffer_8 (Sub, multiplexer_2_out);
  and and_2 (and_2_out, decoder_1_out3, JAL);
  buf buffer_9 (ALU_Out_Ld, and_2_out);
  buf buffer_10 (custom_ALU_Op, and_2_out);
  Multiplexer #(.width(2), .enable("false")) multiplexer_3 (
    .in1(2'b10), .out(multiplexer_3_out), .sel(and_2_out));  // open: in0
  assign ALU_Src2 = multiplexer_3_out;  // Buffer buffer_11, 2 bits wide
  or or_1 (or_1_out, I_Type, OP);
  and and_3 (and_3_out, decoder_1_out4, or_1_out);
  buf buffer_12 (Reg_Write, and_3_out);
  buf buffer_13 (PC_Load, and_3_out);
  buf buffer_14 (PC_Src, and_3_out);
  buf buffer_15 (Reg_Src_2, and_3_out);
  buf buffer_16 (custom_ALU_Op, and_3_out);
  Pull_Resistor pull_resistor_1 (.node(custom_ALU_Op));
  Decoder #(.select(3), .enable("false")) decoder_2 (
    .out0(decoder_2_out0), .out1(decoder_2_out1), .out4(decoder_2_out4), .out5(decoder_2_out5),
    .out6(decoder_2_out6), .out7(decoder_2_out7), .sel(inst_in[14:12]));  // open: out2, out3
  Decoder #(.select(3), .enable("false")) decoder_3 (
    .out0(decoder_3_out0), .out4(decoder_3_out4), .out6(decoder_3_out6), .sel(inst_in[14:12]));  // open: out1, out2, out3, out5, out7
  assign bit_extender_1_out = {{1{1'b0}}, and_1_out};  // Bit_Extender bit_extender_1
  assign ALU_Src2 = bit_extender_1_out;  // Buffer buffer_17, 2 bits wide
  Pull_Resistor pull_resistor_2 (.node(custom_bus_ALU_Op[2]));
  Pull_Resistor pull_resistor_3 (.node(ALU_Src1));
  Pull_Resistor pull_resistor_4 (.node(ALU_Src2));
  Pull_Resistor pull_resistor_5 (.node(PC_Src));
  Pull_Resistor pull_resistor_6 (.node(Sub));
  Pull_Resistor pull_resistor_7 (.node(I_Or_D));
  Pull_Resistor pull_resistor_8 (.node(Mem_Read));
  Pull_Resistor pull_resistor_9 (.node(IR_Load));
  Pull_Resistor pull_resistor_10 (.node(ALU_Out_Ld));
  Pull_Resistor pull_resistor_11 (.node(A_Load));
  Pull_Resistor pull_resistor_12 (.node(B_Load));
  Pull_Resistor pull_resistor_13 (.node(rs1));
  Pull_Resistor pull_resistor_14 (.node(Mem2Reg));
  Pull_Resistor pull_resistor_15 (.node(Reg_Write));
  Pull_Resistor pull_resistor_16 (.node(Reg_Src_2));
  Pull_Resistor pull_resistor_17 (.node(PC_Load));
  Pull_Resistor pull_resistor_18 (.node(mdr_load));
  Pull_Resistor pull_resistor_19 (.node(Mem_Write));
  Pull_Resistor pull_resistor_20 (.node(Sub_in));
  Pull_Resistor pull_resistor_21 (.node(Width));
  Pull_Resistor pull_resistor_22 (.node(extend));
  assign rs1 = inst_in[19:15];  // Buffer buffer_18, 5 bits wide
  or or_2 (or_2_out, decoder_2_out0, decoder_2_out1);
  or or_3 (or_3_out, decoder_2_out4, decoder_2_out5);
  or or_4 (or_4_out, decoder_2_out6, decoder_2_out7);
  or or_5 (branch_z, decoder_3_out0, decoder_3_out4, decoder_3_out6);
  buf buffer_19 (IR_Load, decoder_1_out0);
  buf buffer_20 (ALU_Out_Ld, and_4_out);
  and and_4 (and_4_out, decoder_1_out1, JAL);
  buf buffer_21 (custom_ALU_Op, and_4_out);
  Multiplexer #(.width(2), .enable("false")) multiplexer_4 (
    .in1(2'b10), .out(multiplexer_4_out), .sel(and_4_out));  // open: in0
  assign ALU_Src2 = multiplexer_4_out;  // Buffer buffer_22, 2 bits wide
  and and_5 (and_5_out, decoder_1_out3, JALR);
  and and_6 (and_6_out, decoder_1_out4, or_6_out);
  Pull_Resistor pull_resistor_23 (.node(custom_bus_ALU_Op[0]));
  Pull_Resistor pull_resistor_24 (.node(custom_bus_ALU_Op[1]));
  assign bit_extender_2_out = {{2{or_2_out}}, or_2_out};  // Bit_Extender bit_extender_2
  assign and_7_out = bit_extender_2_out & 3'b100;  // AND_Gate and_7, 3 bits wide
  assign bit_extender_3_out = {{2{or_3_out}}, or_3_out};  // Bit_Extender bit_extender_3
  assign and_8_out = bit_extender_3_out & 3'b010;  // AND_Gate and_8, 3 bits wide
  assign bit_extender_4_out = {{2{or_4_out}}, or_4_out};  // Bit_Extender bit_extender_4
  assign and_9_out = bit_extender_4_out & 3'b011;  // AND_Gate and_9, 3 bits wide
  buf buffer_23 (custom_ALU_Op, decoder_1_out0);
  and and_10 (and_10_out, decoder_1_out2, I_Type);
  buf buffer_24 (ALU_Out_Ld, and_10_out);
  buf buffer_25 (ALU_Src1, and_10_out);
  and and_11 (and_11_out, xnor_1_out[0], xnor_1_out[1], xnor_1_out[2]);
  and and_12 (and_12_out, and_10_out, and_11_out);
  not not_1 (not_1_out, and_12_out);
  Multiplexer #(.enable("false")) multiplexer_5 (.in1(Sub_in), .out(multiplexer_5_out), .sel(not_1_out));  // open: in0
  buf buffer_26 (Sub, multiplexer_5_out);
  buf buffer_27 (ALU_Out_Ld, and_5_out);
  buf buffer_28 (ALU_Src1, and_5_out);
  buf buffer_29 (custom_ALU_Op, and_5_out);
  Multiplexer #(.width(2), .enable("false")) multiplexer_6 (
    .in1(2'b10), .out(multiplexer_6_out), .sel(and_5_out));  // open: in0
  assign ALU_Src2 = multiplexer_6_out;  // Buffer buffer_30, 2 bits wide
  or or_6 (or_6_out, JAL, JALR);
  buf buffer_31 (PC_Load, and_6_out);
  buf buffer_32 (custom_ALU_Op, and_6_out);
  assign branch_type = and_7_out | and_8_out | and_9_out;  // OR_Gate or_7, 3 bits wide
  and and_13 (and_13_out, decoder_1_out1, or_8_out);
  assign xnor_1_out = ~(inst_in[14:12] ^ 3'b101);  // XNOR_Gate xnor_1, 3 bits wide
  Multiplexer #(.enable("false")) multiplexer_7 (
    .in1(Sub_in_srai), .out(multiplexer_7_out), .sel(and_12_out));  // open: in0
  buf buffer_33 (Sub, multiplexer_7_out);
  and and_14 (and_14_out, decoder_1_out3, LOAD);
  and and_15 (and_15_out, decoder_1_out4, or_9_out);
  buf buffer_34 (ALU_Out_Ld, decoder_1_out0);
  or or_8 (or_8_out, LOAD, JALR, STORE);
  buf buffer_35 (A_Load, and_13_out);
  and and_16 (and_16_out, decoder_1_out2, JAL);
  buf buffer_36 (Mem_Read, and_14_out);
  buf buffer_37 (mdr_load, and_14_out);
  buf buffer_38 (I_Or_D, and_14_out);
  or or_9 (or_9_out, LUI, AUIPC);
  buf buffer_39 (PC_Load, and_15_out);
  buf buffer_40 (PC_Src, and_15_out);
  buf buffer_41 (custom_ALU_Op, and_15_out);
  Pull_Resistor pull_resistor_25 ();  // open: node
  Pull_Resistor pull_resistor_26 ();  // open: node
  or or_10 (I_Type, LOAD, JALR, OP_IMM);
  buf buffer_42 (Reg_Write, and_16_out);
  Multiplexer #(.width(2), .enable("false")) multiplexer_8 (
    .in1(2'b10), .out(multiplexer_8_out), .sel(and_10_out));  // open: in0
  assign ALU_Src2 = multiplexer_8_out;  // Buffer buffer_43, 2 bits wide
  Multiplexer #(.enable("false")) multiplexer_9 (
    .in1(inst_in[14]), .out(multiplexer_9_out), .sel(and_14_out));  // open: in0
  buf buffer_44 (extend, multiplexer_9_out);
  assign Width = multiplexer_10_out;  // Buffer buffer_45, 2 bits wide
  Multiplexer #(.width(2), .enable("false")) multiplexer_10 (
    .in1(inst_in[13:12]), .out(multiplexer_10_out), .sel(and_14_out));  // open: in0
  and and_17 (and_17_out, decoder_1_out4, or_12_out);
  Decoder #(.select(2), .disabled(0)) decoder_4 (
    .out0(decoder_4_out0), .out1(decoder_4_out1), .out3(decoder_4_out3), .sel(inst_in[6:5]), .en(valid_opc));  // open: out2
  and and_18 (and_18_out, decoder_1_out1, BRANCH);
  buf buffer_46 (ALU_Out_Ld, and_18_out);
  buf buffer_47 (custom_ALU_Op, and_18_out);
  buf buffer_48 (PC_Load, and_18_out);
  Multiplexer #(.width(2), .enable("false")) multiplexer_11 (
    .in1(2'b10), .out(multiplexer_11_out), .sel(and_18_out));  // open: in0
  assign ALU_Src2 = multiplexer_11_out;  // Buffer buffer_49, 2 bits wide
  or or_11 (or_11_out, SYSTEM, LUI);
  and and_19 (and_19_out, decoder_1_out2, or_11_out);
  buf buffer_50 (ALU_Out_Ld, and_19_out);
  buf buffer_51 (ALU_Src1, and_19_out);
  buf buffer_52 (custom_ALU_Op, and_19_out);
  Multiplexer #(.width(2), .enable("false")) multiplexer_12 (
    .in1(2'b10), .out(multiplexer_12_out), .sel(and_19_out));  // open: in0
  assign ALU_Src2 = multiplexer_12_out;  // Buffer buffer_53, 2 bits wide
  and and_20 (and_20_out, decoder_1_out3, STORE);
  buf buffer_54 (Mem_Read, and_20_out);
  buf buffer_55 (I_Or_D, and_20_out);
  or or_12 (or_12_out, LOAD, STORE);
  buf buffer_56 (Mem2Reg, and_17_out);
  buf buffer_57 (Reg_Write, and_17_out);
  buf buffer_58 (custom_ALU_Op, and_17_out);
  and and_21 (valid_opc, inst_in[0], inst_in[1]);
  Multiplexer #(.width(2), .enable("false")) multiplexer_13 (
    .in1(inst_in[13:12]), .out(multiplexer_13_out), .sel(and_20_out));  // open: in0
  Decoder #(.select(3), .disabled(0)) decoder_5 (
    .out0(decoder_5_out0), .out1(decoder_5_out1), .out3(decoder_5_out3), .out4(decoder_5_out4),
    .out5(decoder_5_out5), .sel(inst_in[4:2]), .en(valid_opc));  // open: out2, out6, out7
  and and_22 (LOAD, decoder_4_out0, decoder_5_out0);
  and and_23 (STORE, decoder_4_out1, decoder_5_out0);
  and and_24 (BRANCH, decoder_4_out3, decoder_5_out0);
  and and_25 (halt, Decode, nor_1_out);
  nor nor_1 (nor_1_out, MISC_MEM, LOAD, OP_IMM, AUIPC, STORE, OP, LUI, BRANCH, JALR, JAL, SYSTEM);
  and and_26 (and_26_out, decoder_1_out1, STORE);
  buf buffer_59 (B_Load, and_26_out);
  and and_27 (and_27_out, decoder_1_out2, AUIPC);
  Multiplexer #(.width(2), .enable("false")) multiplexer_14 (
    .in1(2'b10), .out(multiplexer_14_out), .sel(and_27_out));  // open: in0
  assign ALU_Src2 = multiplexer_14_out;  // Buffer buffer_60, 2 bits wide
  and and_28 (and_28_out, decoder_1_out3, or_13_out);
  assign Width = multiplexer_13_out;  // Buffer buffer_61, 2 bits wide
  and and_29 (and_29_out, decoder_1_out4, SYSTEM);
  buf buffer_62 (tty_write, and_29_out);
  buf buffer_63 (PC_Load, and_29_out);
  buf buffer_64 (PC_Src, and_29_out);
  buf buffer_65 (custom_ALU_Op, and_29_out);
  assign tty_input = multiplexer_15_out;  // Buffer buffer_66, 7 bits wide
  Multiplexer #(.width(7), .enable("false")) multiplexer_15 (
    .in1(alu_out[6:0]), .out(multiplexer_15_out), .sel(and_29_out));  // open: in0
  and and_30 (OP_IMM, decoder_4_out0, decoder_5_out4);
  and and_31 (MISC_MEM, decoder_4_out0, decoder_5_out3);
  and and_32 (OP, decoder_4_out1, decoder_5_out4);
  and and_33 (LUI, decoder_4_out1, decoder_5_out5);
  and and_34 (JALR, decoder_5_out1, decoder_4_out3);
  and and_35 (JAL, decoder_5_out3, decoder_4_out3);
  buf buffer_67 (ALU_Out_Ld, and_27_out);
  buf buffer_68 (custom_ALU_Op, and_27_out);
  or or_13 (or_13_out, OP_IMM, LUI, OP);
  buf buffer_69 (Reg_Write, and_28_out);
  and and_36 (AUIPC, decoder_4_out0, decoder_5_out5);
  and and_37 (SYSTEM, decoder_5_out4, decoder_4_out3);
  and and_38 (and_38_out, decoder_1_out1, SYSTEM);
  buf buffer_70 (A_Load, and_38_out);
  Multiplexer #(.width(5), .enable("false")) multiplexer_16 (
    .in1(5'b01010), .out(multiplexer_16_out), .sel(and_38_out));  // open: in0
  assign rs1 = multiplexer_16_out;  // Buffer buffer_71, 5 bits wide
  or or_14 (or_14_out, LOAD, STORE);
  and and_39 (and_39_out, decoder_1_out2, or_14_out);
  buf buffer_72 (ALU_Out_Ld, and_39_out);
  buf buffer_73 (ALU_Src1, and_39_out);
  assign bit_extender_5_out = {{1{1'b0}}, and_39_out};  // Bit_Extender bit_extender_5
  buf buffer_74 (custom_ALU_Op, and_39_out);
  assign ALU_Src2 = bit_extender_5_out;  // Buffer buffer_75, 2 bits wide
  or or_15 (U_Type, AUIPC, LUI);
  Pull_Resistor pull_resistor_27 (.node(tty_input));
  TTY tty_1 (.data(tty_input), .clk(clk), .we(tty_write));  // open: clr
  Pull_Resistor pull_resistor_28 (.node(tty_write));
  and and_40 (and_40_out, decoder_1_out2, BRANCH);
  or or_16 (or_16_out, AUIPC, LUI);
  assign bit_extender_6_out = {{19{BRANCH}}, BRANCH};  // Bit_Extender bit_extender_6
  buf buffer_76 (ALU_Src1, and_40_out);
  buf buffer_77 (Sub, and_40_out);
  buf buffer_78 (custom_ALU_Op, and_40_out);
  Multiplexer #(.width(3), .enable("false")) multiplexer_17 (
    .in1(branch_type), .out(multiplexer_17_out), .sel(and_40_out));  // open: in0
  assign custom_bus_ALU_Op = multiplexer_17_out;  // Buffer buffer_79, 3 bits wide
  assign bit_extender_7_out = {{19{or_16_out}}, or_16_out};  // Bit_Extender bit_extender_7
  assign bit_extender_8_out = {{19{STORE}}, STORE};  // Bit_Extender bit_extender_8
  assign bit_extender_9_out = {{19{I_Type}}, I_Type};  // Bit_Extender bit_extender_9
  assign and_41_out = {inst_in[31], inst_in[19:12], inst_in[20], inst_in[30:21]} & bit_extender_10_out;  // AND_Gate and_41, 20 bits wide
  assign bit_extender_10_out = {{19{JAL}}, JAL};  // Bit_Extender bit_extender_10
  assign and_42_out = imm_sb & bit_extender_6_out;  // AND_Gate and_42, 20 bits wide
  xnor xnor_2 (xnor_2_out, z_in, branch_z);
  and and_43 (and_43_out, and_40_out, xnor_2_out);
  assign and_44_out = inst_in[31:12] & bit_extender_7_out;  // AND_Gate and_44, 20 bits wide
  assign and_45_out = imm_s & bit_extender_8_out;  // AND_Gate and_45, 20 bits wide
  assign and_46_out = imm_i & bit_extender_9_out;  // AND_Gate and_46, 20 bits wide
  buf buffer_80 (PC_Load, and_43_out);
  assign or_17_out = and_44_out | and_45_out | and_46_out;  // OR_Gate or_17, 20 bits wide
  assign or_18_out = and_41_out | and_42_out;  // OR_Gate or_18, 20 bits wide
  assign bit_extender_11_out = {{11{or_18_out[19]}}, or_18_out};  // Bit_Extender bit_extender_11
  assign bit_extender_12_out = {{12{or_17_out[19]}}, or_17_out};  // Bit_Extender bit_extender_12
  Multiplexer #(.width(2), .enable("false")) multiplexer_18 (
    .in1(2'b01), .out(multiplexer_18_out), .sel(and_40_out));  // open: in0
  assign ALU_Src2 = multiplexer_18_out;  // Buffer buffer_81, 2 bits wide
  assign imm = bit_extender_12_out | {bit_extender_11_out, 1'b0};  // OR_Gate or_19, 32 bits wide
  assign {bit_extender_13_out[19], Sub_in_srai, bit_extender_13_out[17:0]} = {{8{inst_in[31]}}, inst_in[31:20]};  // Bit_Extender bit_extender_13
  assign imm_s = {{8{inst_in[31]}}, {inst_in[31:25], inst_in[11:7]}};  // Bit_Extender bit_extender_14
  assign imm_sb = {{8{inst_in[31]}}, {inst_in[31], inst_in[7], inst_in[30:25], inst_in[11:8]}};  // Bit_Extender bit_extender_15
  Multiplexer #(.width(20), .enable("false")) multiplexer_19 (
    .in0({bit_extender_13_out[19], Sub_in_srai, bit_extender_13_out[17:0]}),
    .in1({bit_extender_13_out[19], 1'b0, bit_extender_13_out[17:0]}), .out(imm_i), .sel(and_47_out));
  and and_47 (and_47_out, xnor_3_out[0], xnor_3_out[1], xnor_3_out[2]);
  assign xnor_3_out = ~(inst_in[14:12] ^ 3'b101);  // XNOR_Gate xnor_3, 3 bits wide

  assign rd = inst_in[11:7];
  assign rs2 = inst_in[24:20];

  // Other names for the same wires on the sheet: inst[31:0] = inst_in; funct7[6:0] = inst_in[31:25];
  //   imm_u[19:0] = inst_in[31:12]; imm_uj[19:0] = {inst_in[31], inst_in[19:12], inst_in[20], inst_in[30:21]};
  //   c = c_in; funct3[2:0] = inst_in[14:12]; inst_4_2[2:0] = inst_in[4:2]; inst_6_5[1:0] = inst_in[6:5];
  //   Mdr_Ld = mdr_load; sub_out = Sub; z = z_in

  // Notes on the sheet:
  //   buffer_1 drives only 1 and floats otherwise
  //   buffer_3 drives only 1 and floats otherwise
  //   buffer_4 drives only 1 and floats otherwise
  //   buffer_5 drives only 1 and floats otherwise
  //   buffer_6 drives only 1 and floats otherwise
  //   buffer_7 drives only 1 and floats otherwise
  //   buffer_8 drives only 1 and floats otherwise
  //   buffer_9 drives only 1 and floats otherwise
  //   buffer_10 drives only 1 and floats otherwise
  //   buffer_11 drives only 1 and floats otherwise
  //   buffer_12 drives only 1 and floats otherwise
  //   buffer_13 drives only 1 and floats otherwise
  //   buffer_14 drives only 1 and floats otherwise
  //   buffer_15 drives only 1 and floats otherwise
  //   buffer_16 drives only 1 and floats otherwise
  //   buffer_17 drives only 1 and floats otherwise
  //   buffer_18 drives only 1 and floats otherwise
  //   buffer_19 drives only 1 and floats otherwise
  //   buffer_20 drives only 1 and floats otherwise
  //   buffer_21 drives only 1 and floats otherwise
  //   buffer_22 drives only 1 and floats otherwise
  //   buffer_23 drives only 1 and floats otherwise
  //   buffer_24 drives only 1 and floats otherwise
  //   buffer_25 drives only 1 and floats otherwise
  //   buffer_26 drives only 1 and floats otherwise
  //   buffer_27 drives only 1 and floats otherwise
  //   buffer_28 drives only 1 and floats otherwise
  //   buffer_29 drives only 1 and floats otherwise
  //   buffer_30 drives only 1 and floats otherwise
  //   buffer_31 drives only 1 and floats otherwise
  //   buffer_32 drives only 1 and floats otherwise
  //   buffer_33 drives only 1 and floats otherwise
  //   buffer_34 drives only 1 and floats otherwise
  //   buffer_35 drives only 1 and floats otherwise
  //   buffer_36 drives only 1 and floats otherwise
  //   buffer_37 drives only 1 and floats otherwise
  //   buffer_38 drives only 1 and floats otherwise
  //   buffer_39 drives only 1 and floats otherwise
  //   buffer_40 drives only 1 and floats otherwise
  //   buffer_41 drives only 1 and floats otherwise
  //   buffer_42 drives only 1 and floats otherwise
  //   buffer_43 drives only 1 and floats otherwise
  //   buffer_44 drives only 1 and floats otherwise
  //   buffer_45 drives only 1 and floats otherwise
  //   buffer_46 drives only 1 and floats otherwise
  //   buffer_47 drives only 1 and floats otherwise
  //   buffer_48 drives only 1 and floats otherwise
  //   buffer_49 drives only 1 and floats otherwise
  //   buffer_50 drives only 1 and floats otherwise
  //   buffer_51 drives only 1 and floats otherwise
  //   buffer_52 drives only 1 and floats otherwise
  //   buffer_53 drives only 1 and floats otherwise
  //   buffer_54 drives only 1 and floats otherwise
  //   buffer_55 drives only 1 and floats otherwise
  //   buffer_56 drives only 1 and floats otherwise
  //   buffer_57 drives only 1 and floats otherwise
  //   buffer_58 drives only 1 and floats otherwise
  //   buffer_59 drives only 1 and floats otherwise
  //   buffer_60 drives only 1 and floats otherwise
  //   buffer_61 drives only 1 and floats otherwise
  //   buffer_62 drives only 1 and floats otherwise
  //   buffer_63 drives only 1 and floats otherwise
  //   buffer_64 drives only 1 and floats otherwise
  //   buffer_65 drives only 1 and floats otherwise
  //   buffer_66 drives only 1 and floats otherwise
  //   buffer_67 drives only 1 and floats otherwise
  //   buffer_68 drives only 1 and floats otherwise
  //   buffer_69 drives only 1 and floats otherwise
  //   buffer_70 drives only 1 and floats otherwise
  //   buffer_71 drives only 1 and floats otherwise
  //   buffer_72 drives only 1 and floats otherwise
  //   buffer_73 drives only 1 and floats otherwise
  //   buffer_74 drives only 1 and floats otherwise
  //   buffer_75 drives only 1 and floats otherwise
  //   buffer_76 drives only 1 and floats otherwise
  //   buffer_77 drives only 1 and floats otherwise
  //   buffer_78 drives only 1 and floats otherwise
  //   buffer_79 drives only 1 and floats otherwise
  //   buffer_80 drives only 1 and floats otherwise
  //   buffer_81 drives only 1 and floats otherwise
endmodule
