// Logisim project cpu revised.circ as structural Verilog: 1 circuit, main circuit main
module main (
  input  in_1,
  output halt
);

  wire clock_1_out, control_unit_1_a_load, control_unit_1_alu_out_ld, control_unit_1_alu_src1,
       control_unit_1_b_load, control_unit_1_extend, control_unit_1_i_or_d, control_unit_1_ir_load,
       control_unit_1_mdr_load, control_unit_1_mem2reg, control_unit_1_mem_read, control_unit_1_mem_write,
       control_unit_1_pc_load, control_unit_1_pc_src, control_unit_1_reg_src_2, control_unit_1_reg_write,
       control_unit_1_sub, main_1_carry_out, main_1_zero, pull_resistor_1_node;
  wire [1:0] control_unit_1_alu_src2, control_unit_1_width;
  wire [2:0] control_unit_1_alu_op;
  wire [4:0] control_unit_1_rd, control_unit_1_rs1, control_unit_1_rs2;
  wire [31:0] control_unit_1_imm, main_1_aluout, main_1_inst;

  Pull_Resistor pull_resistor_1 (.node(pull_resistor_1_node));
  data_path_main main_1 (
    .Pc_Src(control_unit_1_pc_src), .PC_Load(control_unit_1_pc_load), .I_Or_D(control_unit_1_i_or_d),
    .MDR_Load(control_unit_1_mdr_load), .ALoad(control_unit_1_a_load), .RegWrite(control_unit_1_reg_write),
    .Rs2(control_unit_1_rs2), .BLoad(control_unit_1_b_load), .Rd(control_unit_1_rd),
    .Imm(control_unit_1_imm), .Alu_Out_Ld(control_unit_1_alu_out_ld), .Clk(clock_1_out), .Carry_In(in_1),
    .SUB(control_unit_1_sub), .MemWr(control_unit_1_mem_write), .Width(control_unit_1_width),
    .Extend(control_unit_1_extend), .MemRd(control_unit_1_mem_read), .clear(pull_resistor_1_node),
    .IRLoad(control_unit_1_ir_load), .Mem2Reg(control_unit_1_mem2reg), .RegSrc2(control_unit_1_reg_src_2),
    .Rs1(control_unit_1_rs1), .ALU_Src1(control_unit_1_alu_src1), .ALUSrc2(control_unit_1_alu_src2),
    .OP(control_unit_1_alu_op), .ALUOut(main_1_aluout), .Carry_Out(main_1_carry_out), .Zero(main_1_zero),
    .inst(main_1_inst));
  Clock clock_1 (.out(clock_1_out));
  control_unit control_unit_1 (
    .clk(clock_1_out), .ALU_Op(control_unit_1_alu_op), .inst_in(main_1_inst), .alu_out(main_1_aluout),
    .ALU_Src1(control_unit_1_alu_src1), .z_in(main_1_zero), .ALU_Src2(control_unit_1_alu_src2),
    .c_in(main_1_carry_out), .PC_Src(control_unit_1_pc_src), .rs2(control_unit_1_rs2),
    .Sub(control_unit_1_sub), .rd(control_unit_1_rd), .I_Or_D(control_unit_1_i_or_d),
    .Mem2Reg(control_unit_1_mem2reg), .Mem_Read(control_unit_1_mem_read),
    .Reg_Write(control_unit_1_reg_write), .IR_Load(control_unit_1_ir_load),
    .Reg_Src_2(control_unit_1_reg_src_2), .imm(control_unit_1_imm), .PC_Load(control_unit_1_pc_load),
    .ALU_Out_Ld(control_unit_1_alu_out_ld), .mdr_load(control_unit_1_mdr_load),
    .A_Load(control_unit_1_a_load), .Mem_Write(control_unit_1_mem_write), .B_Load(control_unit_1_b_load),
    .rs1(control_unit_1_rs1), .Width(control_unit_1_width), .extend(control_unit_1_extend), .halt(halt));
endmodule
