// Logisim project cpu.circ as structural Verilog: 1 circuit, main circuit main
module main (
  input  C_in,
  input  Sub_in,
  output Carry_Out,
  output halt
);

  wire clock_1_out, main_2_a_load, main_2_alu_out_ld, main_2_alu_src1, main_2_b_load, main_2_extend,
       main_2_i_or_d, main_2_ir_load, main_2_mdr_load, main_2_mem2reg, main_2_mem_read, main_2_mem_write,
       main_2_pc_load, main_2_pc_src, main_2_reg_src_2, main_2_reg_write, main_2_sub, Z_in;
  wire [1:0] main_2_alu_src2, main_2_width;
  wire [2:0] main_2_alu_op;
  wire [4:0] main_2_rd, main_2_rs1, main_2_rs2;
  wire [31:0] main_1_aluout, main_1_inst, main_2_imm;

  data_path_main main_1 (
    .Pc_Src(main_2_pc_src), .PC_Load(main_2_pc_load), .I_Or_D(main_2_i_or_d), .MDR_Load(main_2_mdr_load),
    .ALoad(main_2_a_load), .RegWrite(main_2_reg_write), .Rs2(main_2_rs2), .BLoad(main_2_b_load),
    .Rd(main_2_rd), .Imm(main_2_imm), .Alu_Out_Ld(main_2_alu_out_ld), .Clk(clock_1_out), .Carry_In(1'b0),
    .SUB(main_2_sub), .MemWr(main_2_mem_write), .Width(main_2_width), .Extend(main_2_extend),
    .MemRd(main_2_mem_read), .clear(1'b0), .IRLoad(main_2_ir_load), .Mem2Reg(main_2_mem2reg),
    .RegSrc2(main_2_reg_src_2), .Rs1(main_2_rs1), .ALU_Src1(main_2_alu_src1), .ALUSrc2(main_2_alu_src2),
    .OP(main_2_alu_op), .ALUOut(main_1_aluout), .Carry_Out(Carry_Out), .Zero(Z_in), .inst(main_1_inst));
  Clock clock_1 (.out(clock_1_out));
  control_unit_revised_main main_2 (
    .clk(clock_1_out), .ALU_Op(main_2_alu_op), .ALU_Src1(main_2_alu_src1), .ALU_Src2(main_2_alu_src2),
    .alu_out(main_1_aluout), .PC_Src(main_2_pc_src), .Sub(main_2_sub), .I_Or_D(main_2_i_or_d),
    .Mem_Read(main_2_mem_read), .inst_in(main_1_inst), .IR_Load(main_2_ir_load), .imm(main_2_imm),
    .ALU_Out_Ld(main_2_alu_out_ld), .A_Load(main_2_a_load), .z_in(Z_in), .B_Load(main_2_b_load), .c_in(C_in),
    .rs1(main_2_rs1), .rs2(main_2_rs2), .rd(main_2_rd), .Mem2Reg(main_2_mem2reg),
    .Reg_Write(main_2_reg_write), .Reg_Src_2(main_2_reg_src_2), .PC_Load(main_2_pc_load),
    .mdr_load(main_2_mdr_load), .Mem_Write(main_2_mem_write), .Sub_in(Sub_in), .Width(main_2_width),
    .extend(main_2_extend), .halt(halt));

  // Other names for the same wires on the sheet: Zero = Z_in
endmodule
