// Logisim project data path.circ as structural Verilog: 1 circuit, main circuit main
module main (
  input  Clk,
  input  Pc_Src,
  input  PC_Load,
  input  I_Or_D,
  input  SUB,
  input  Carry_In,
  input  MDR_Load,
  input  Mem2Reg,
  input  ALoad,
  input  ALU_Src1,
  input  RegWrite,
  input  [2:0] OP,
  input  [4:0] Rs2,
  input  BLoad,
  input  IRLoad,
  input  [4:0] Rd,
  input  [4:0] Rs1,
  input  RegSrc2,
  input  [1:0] ALUSrc2,
  input  [31:0] Imm,
  input  Alu_Out_Ld,
  input  MemWr,
  input  [1:0] Width,
  input  Extend,
  input  MemRd,
  input  clear,
  output Carry_Out,
  output Zero,
  output [31:0] inst,
  output [31:0] ALUOut
);

  wire memory_1_p7;
  wire [4:0] multiplexer_4_out;
  wire [31:0] A_q, alu_1_ouput, B, main_1_output1, main_1_output2, MDR_q, memory_1_p10, multiplexer_1_out,
       multiplexer_2_out, multiplexer_3_out, multiplexer_5_out, multiplexer_6_out, PC_q, subtractor_1_out;

  Multiplexer #(.width(32)) multiplexer_1 (
    .in0(ALUOut), .in1(alu_1_ouput), .out(multiplexer_1_out), .sel(Pc_Src));  // open: en
  Register #(.width(32)) PC (.D(multiplexer_1_out), .en(PC_Load), .Q(PC_q), .clk(Clk));  // open: clr
  Multiplexer #(.width(32), .enable("false")) multiplexer_2 (
    .in0(PC_q), .in1(ALUOut), .out(multiplexer_2_out), .sel(I_Or_D));
  // Memory memory_1: pin names not known; wires that end beside it: multiplexer_2_out, B, MemWr, Width, Extend, Clk, memory_1_p7, MemRd, clear, memory_1_p10, inst
  Register #(.width(32)) MDR (.D(memory_1_p10), .en(MDR_Load), .Q(MDR_q), .clk(memory_1_p7));  // open: clr
  Register #(.width(32)) IR (.D(memory_1_p10), .en(IRLoad), .Q(inst), .clk(memory_1_p7));  // open: clr
  Multiplexer #(.width(32), .enable("false")) multiplexer_3 (
    .in0(ALUOut), .in1(MDR_q), .out(multiplexer_3_out), .sel(Mem2Reg));
  Multiplexer #(.width(5), .enable("false")) multiplexer_4 (
    .in0(Rs2), .in1(Rd), .out(multiplexer_4_out), .sel(RegSrc2));
  register_revised_main main_1 (
    .enable(RegWrite), .Clock(Clk), .write_data(multiplexer_3_out), .write_address(Rd), .raddr1(Rs1),
    .raddr2(multiplexer_4_out), .Output1(main_1_output1), .Output2(main_1_output2));
  Register #(.width(32)) A (.D(main_1_output1), .en(ALoad), .Q(A_q), .clk(Clk));  // open: clr
  Register #(.width(32)) u_B (.D(main_1_output2), .en(BLoad), .Q(B), .clk(Clk));  // open: clr
  Subtractor #(.width(32)) subtractor_1 (.a(Imm), .b(32'h4), .out(subtractor_1_out));  // open: bin, bout
  Multiplexer #(.width(32)) multiplexer_5 (.in0(PC_q), .in1(A_q), .out(multiplexer_5_out), .sel(ALU_Src1));  // open: en
  Multiplexer #(.select(2), .width(32)) multiplexer_6 (
    .in0(32'h4), .in1(B), .in2(Imm), .in3(subtractor_1_out), .out(multiplexer_6_out), .sel(ALUSrc2));  // open: en
  ALU alu_1 (
    .Input_1(multiplexer_5_out), .Input_2(multiplexer_6_out), .carry_in(Carry_In), .Op(SUB), .select(OP),
    .carry_out(Carry_Out), .Ouput(alu_1_ouput), .Zero(Zero));
  Register #(.width(32)) u_ALUOut (.D(alu_1_ouput), .en(Alu_Out_Ld), .Q(ALUOut), .clk(memory_1_p7));  // open: clr
endmodule
