// Logisim project register revised.circ as structural Verilog: 1 circuit, main circuit main
module main (
  input  Clock,
  input  [31:0] write_data,
  input  [4:0] raddr1,
  input  enable,
  input  [4:0] write_address,
  input  [4:0] raddr2,
  output [31:0] Output1,
  output [31:0] Output2
);

  wire demultiplexer_1_out0, demultiplexer_1_out1, demultiplexer_1_out2, demultiplexer_1_out3,
       demultiplexer_1_out4, demultiplexer_1_out5, demultiplexer_1_out6, demultiplexer_1_out7,
       demultiplexer_1_out8, demultiplexer_1_out9, demultiplexer_1_out10, demultiplexer_1_out11,
       demultiplexer_1_out12, demultiplexer_1_out13, demultiplexer_1_out14, demultiplexer_1_out15,
       demultiplexer_1_out16, demultiplexer_1_out17, demultiplexer_1_out18, demultiplexer_1_out19,
       demultiplexer_1_out20, demultiplexer_1_out21, demultiplexer_1_out22, demultiplexer_1_out23,
       demultiplexer_1_out24, demultiplexer_1_out25, demultiplexer_1_out26, demultiplexer_1_out27,
       demultiplexer_1_out28, demultiplexer_1_out29, demultiplexer_1_out30, demultiplexer_1_out31;
  wire [31:0] _0, _1, _2, _3, _4, _5, _6, _7, _8, _9, _10, _11, _12, _13, _14, _15, _16, _17, _18, _19, _20,
       _21, _22, _23, _24, _25, _26, _27, _28, _29, _30, _31;

  Demultiplexer #(.select(5)) demultiplexer_1 (
    .out0(demultiplexer_1_out0), .out1(demultiplexer_1_out1), .out2(demultiplexer_1_out2),
    .out3(demultiplexer_1_out3), .out4(demultiplexer_1_out4), .out5(demultiplexer_1_out5),
    .out6(demultiplexer_1_out6), .out7(demultiplexer_1_out7), .out8(demultiplexer_1_out8),
    .out9(demultiplexer_1_out9), .out10(demultiplexer_1_out10), .out11(demultiplexer_1_out11),
    .out12(demultiplexer_1_out12), .out13(demultiplexer_1_out13), .out14(demultiplexer_1_out14),
    .out15(demultiplexer_1_out15), .out16(demultiplexer_1_out16), .out17(demultiplexer_1_out17),
    .out18(demultiplexer_1_out18), .out19(demultiplexer_1_out19), .out20(demultiplexer_1_out20),
    .out21(demultiplexer_1_out21), .out22(demultiplexer_1_out22), .out23(demultiplexer_1_out23),
    .out24(demultiplexer_1_out24), .out25(demultiplexer_1_out25), .out26(demultiplexer_1_out26),
    .out27(demultiplexer_1_out27), .out28(demultiplexer_1_out28), .out29(demultiplexer_1_out29),
    .out30(demultiplexer_1_out30), .out31(demultiplexer_1_out31), .in(enable), .sel(write_address));  // open: en
  Register #(.width(32)) register_1 (.D(write_data), .en(demultiplexer_1_out0), .Q(_0), .clk(Clock));  // open: clr
  Register #(.width(32)) register_2 (.D(write_data), .en(demultiplexer_1_out1), .Q(_1), .clk(Clock));  // open: clr
  Register #(.width(32)) register_3 (.D(write_data), .en(demultiplexer_1_out2), .Q(_2), .clk(Clock));  // open: clr
  Register #(.width(32)) register_4 (.D(write_data), .en(demultiplexer_1_out3), .Q(_3), .clk(Clock));  // open: clr
  Register #(.width(32)) register_5 (.D(write_data), .en(demultiplexer_1_out4), .Q(_4), .clk(Clock));  // open: clr
  Register #(.width(32)) register_6 (.D(write_data), .en(demultiplexer_1_out5), .Q(_5), .clk(Clock));  // open: clr
  Register #(.width(32)) register_7 (.D(write_data), .en(demultiplexer_1_out6), .Q(_6), .clk(Clock));  // open: clr
  Register #(.width(32)) register_8 (.D(write_data), .en(demultiplexer_1_out7), .Q(_7), .clk(Clock));  // open: clr
  Register #(.width(32)) register_9 (.D(write_data), .en(demultiplexer_1_out8), .Q(_8), .clk(Clock));  // open: clr
  Register #(.width(32)) register_10 (.D(write_data), .en(demultiplexer_1_out9), .Q(_9), .clk(Clock));  // open: clr
  Register #(.width(32)) register_11 (.D(write_data), .en(demultiplexer_1_out10), .Q(_10), .clk(Clock));  // open: clr
  Register #(.width(32)) register_12 (.D(write_data), .en(demultiplexer_1_out11), .Q(_11), .clk(Clock));  // open: clr
  Register #(.width(32)) register_13 (.D(write_data), .en(demultiplexer_1_out12), .Q(_12), .clk(Clock));  // open: clr
  Register #(.width(32)) register_14 (.D(write_data), .en(demultiplexer_1_out13), .Q(_13), .clk(Clock));  // open: clr
  Register #(.width(32)) register_15 (.D(write_data), .en(demultiplexer_1_out14), .Q(_14), .clk(Clock));  // open: clr
  Register #(.width(32)) register_16 (.D(write_data), .en(demultiplexer_1_out15), .Q(_15), .clk(Clock));  // open: clr
  Register #(.width(32)) register_17 (.D(write_data), .en(demultiplexer_1_out16), .Q(_16), .clk(Clock));  // open: clr
  Register #(.width(32)) register_18 (.D(write_data), .en(demultiplexer_1_out17), .Q(_17), .clk(Clock));  // open: clr
  Register #(.width(32)) register_19 (.D(write_data), .en(demultiplexer_1_out18), .Q(_18), .clk(Clock));  // open: clr
  Register #(.width(32)) register_20 (.D(write_data), .en(demultiplexer_1_out19), .Q(_19), .clk(Clock));  // open: clr
  Register #(.width(32)) register_21 (.D(write_data), .en(demultiplexer_1_out20), .Q(_20), .clk(Clock));  // open: clr
  Register #(.width(32)) register_22 (.D(write_data), .en(demultiplexer_1_out21), .Q(_21), .clk(Clock));  // open: clr
  Register #(.width(32)) register_23 (.D(write_data), .en(demultiplexer_1_out22), .Q(_22), .clk(Clock));  // open: clr
  Register #(.width(32)) register_24 (.D(write_data), .en(demultiplexer_1_out23), .Q(_23), .clk(Clock));  // open: clr
  Register #(.width(32)) register_25 (.D(write_data), .en(demultiplexer_1_out24), .Q(_24), .clk(Clock));  // open: clr
  Register #(.width(32)) register_26 (.D(write_data), .en(demultiplexer_1_out25), .Q(_25), .clk(Clock));  // open: clr
  Register #(.width(32)) register_27 (.D(write_data), .en(demultiplexer_1_out26), .Q(_26), .clk(Clock));  // open: clr
  Register #(.width(32)) register_28 (.D(write_data), .en(demultiplexer_1_out27), .Q(_27), .clk(Clock));  // open: clr
  Register #(.width(32)) register_29 (.D(write_data), .en(demultiplexer_1_out28), .Q(_28), .clk(Clock));  // open: clr
  Register #(.width(32)) register_30 (.D(write_data), .en(demultiplexer_1_out29), .Q(_29), .clk(Clock));  // open: clr
  Register #(.width(32)) register_31 (.D(write_data), .en(demultiplexer_1_out30), .Q(_30), .clk(Clock));  // open: clr
  Register #(.width(32)) register_32 (.D(write_data), .en(demultiplexer_1_out31), .Q(_31), .clk(Clock));  // open: clr
  Multiplexer #(.select(5), .width(32)) multiplexer_1 (
    .in0(_0), .in1(_1), .in2(_2), .in3(_3), .in4(_4), .in5(_5), .in6(_6), .in7(_7), .in8(_8), .in9(_9),
    .in10(_10), .in11(_11), .in12(_12), .in13(_13), .in14(_14), .in15(_15), .in16(_16), .in17(_17),
    .in18(_18), .in19(_19), .in20(_20), .in21(_21), .in22(_22), .in23(_23), .in24(_24), .in25(_25),
    .in26(_26), .in27(_27), .in28(_28), .in29(_29), .in30(_30), .in31(_31), .out(Output1), .sel(raddr1));  // open: en
  Multiplexer #(.select(5), .width(32)) multiplexer_2 (
    .in0(_0), .in1(_1), .in2(_2), .in3(_3), .in4(_4), .in5(_5), .in6(_6), .in7(_7), .in8(_8), .in9(_9),
    .in10(_10), .in11(_11), .in12(_12), .in13(_13), .in14(_14), .in15(_15), .in16(_16), .in17(_17),
    .in18(_18), .in19(_19), .in20(_20), .in21(_21), .in22(_22), .in23(_23), .in24(_24), .in25(_25),
    .in26(_26), .in27(_27), .in28(_28), .in29(_29), .in30(_30), .in31(_31), .out(Output2), .sel(raddr2));  // open: en
endmodule
