// Logisim project right shifter.circ as structural Verilog: 1 circuit, main circuit right shift
module right_shift (
  input  [31:0] input_1,
  input  [31:0] input_2,
  input  select_input,
  output [31:0] out_4
);

  wire [4:0] bit_extender_1_out;
  wire [31:0] shifter_1_out, shifter_2_out;

  Shifter #(.width(32), .shift("ar")) shifter_1 (.in(input_1), .\dist (bit_extender_1_out), .out(shifter_1_out));
  Bit_Extender #(.in_width(32), .out_width(5)) bit_extender_1 (.in(input_2), .out(bit_extender_1_out));
  Shifter #(.width(32), .shift("lr")) shifter_2 (.in(input_1), .\dist (bit_extender_1_out), .out(shifter_2_out));
  Multiplexer #(.width(32), .enable("false")) multiplexer_1 (
    .in0(shifter_2_out), .in1(shifter_1_out), .out(out_4), .sel(select_input));
endmodule
