// Logisim project sltu.circ as structural Verilog: 1 circuit, main circuit sltu
module sltu (
  input  [31:0] in_1,
  input  [31:0] in_2,
  input  carry_in,
  output [31:0] out_4,
  output carry_out
);

  wire xor_1_out, xor_2_out;
  wire [31:0] subtractor_1_out;

  Subtractor #(.width(32)) subtractor_1 (.a(in_1), .b(in_2), .out(subtractor_1_out), .bin(carry_in), .bout(carry_out));
  xor xor_1 (xor_1_out, in_1[31], in_2[31]);
  xor xor_2 (xor_2_out, xor_1_out, subtractor_1_out[31]);
  assign out_4 = {{31{1'b0}}, xor_2_out};  // Bit_Extender bit_extender_1
endmodule
